// Logisim project reloginho.circ as structural Verilog: 12 circuits, main circuit main
// 7
module main (
);

  wire clock_1_out, contador0_6_1_a, contador0_6_1_b, contador0_6_1_c, contador0_6_1_clockpass,
       contador0_6_1_d, contador0_6_1_e, contador0_6_1_f, contador0_6_1_g, contador0_6_2_a, contador0_6_2_b,
       contador0_6_2_c, contador0_6_2_clockpass, contador0_6_2_d, contador0_6_2_e, contador0_6_2_f,
       contador0_6_2_g, contador0_9_1_a, contador0_9_1_b, contador0_9_1_c, contador0_9_1_clockpass,
       contador0_9_1_d, contador0_9_1_e, contador0_9_1_f, contador0_9_1_g, contador0_9_2_a, contador0_9_2_b,
       contador0_9_2_c, contador0_9_2_clockpass, contador0_9_2_d, contador0_9_2_e, contador0_9_2_f,
       contador0_9_2_g, contadorhora_1_a, contadorhora_1_a_2, contadorhora_1_b, contadorhora_1_b_2,
       contadorhora_1_c, contadorhora_1_c_2, contadorhora_1_d, contadorhora_1_d_2, contadorhora_1_e,
       contadorhora_1_e_2, contadorhora_1_f, contadorhora_1_f_2, contadorhora_1_g, contadorhora_1_g_2,
       not_1_out;

  _7_Segment_Display u_7_segment_display_1 (
    .g(contadorhora_1_g), .f(contadorhora_1_f), .a(contadorhora_1_a), .b(contadorhora_1_b),
    .e(contadorhora_1_e), .d(contadorhora_1_d), .c(contadorhora_1_c));  // open: dp
  CONTADORHORA contadorhora_1 (
    .clockH(contador0_6_1_clockpass), .G(contadorhora_1_g), .F(contadorhora_1_f), .E(contadorhora_1_e),
    .D(contadorhora_1_d), .C(contadorhora_1_c), .B(contadorhora_1_b), .A(contadorhora_1_a),
    .g_2(contadorhora_1_g_2), .f_2(contadorhora_1_f_2), .e_2(contadorhora_1_e_2), .d_2(contadorhora_1_d_2),
    .c_2(contadorhora_1_c_2), .b_2(contadorhora_1_b_2), .a_2(contadorhora_1_a_2));
  _7_Segment_Display u_7_segment_display_2 (
    .g(contadorhora_1_g_2), .f(contadorhora_1_f_2), .a(contadorhora_1_a_2), .b(contadorhora_1_b_2),
    .e(contadorhora_1_e_2), .d(contadorhora_1_d_2), .c(contadorhora_1_c_2));  // open: dp
  _7_Segment_Display u_7_segment_display_3 (
    .g(contador0_6_1_g), .f(contador0_6_1_f), .a(contador0_6_1_a), .b(contador0_6_1_b), .e(contador0_6_1_e),
    .d(contador0_6_1_d), .c(contador0_6_1_c));  // open: dp
  CONTADOR0_6 contador0_6_1 (
    .clock(contador0_9_1_clockpass), .A(contador0_6_1_a), .B(contador0_6_1_b), .C(contador0_6_1_c),
    .D(contador0_6_1_d), .E(contador0_6_1_e), .F(contador0_6_1_f), .G(contador0_6_1_g),
    .clockpass(contador0_6_1_clockpass));
  _7_Segment_Display u_7_segment_display_4 (
    .g(contador0_9_1_g), .f(contador0_9_1_f), .a(contador0_9_1_a), .b(contador0_9_1_b), .e(contador0_9_1_e),
    .d(contador0_9_1_d), .c(contador0_9_1_c));  // open: dp
  _7_Segment_Display u_7_segment_display_5 (
    .g(contador0_6_2_g), .f(contador0_6_2_f), .a(contador0_6_2_a), .b(contador0_6_2_b), .e(contador0_6_2_e),
    .d(contador0_6_2_d), .c(contador0_6_2_c));  // open: dp
  _7_Segment_Display u_7_segment_display_6 (
    .g(contador0_9_2_g), .f(contador0_9_2_f), .a(contador0_9_2_a), .b(contador0_9_2_b), .e(contador0_9_2_e),
    .d(contador0_9_2_d), .c(contador0_9_2_c));  // open: dp
  CONTADOR0_9 contador0_9_1 (
    .clockglobal(contador0_6_2_clockpass), .clockpass(contador0_9_1_clockpass), .G(contador0_9_1_g),
    .F(contador0_9_1_f), .E(contador0_9_1_e), .D(contador0_9_1_d), .C(contador0_9_1_c), .B(contador0_9_1_b),
    .A(contador0_9_1_a));
  CONTADOR0_6 contador0_6_2 (
    .clock(contador0_9_2_clockpass), .A(contador0_6_2_a), .B(contador0_6_2_b), .C(contador0_6_2_c),
    .D(contador0_6_2_d), .E(contador0_6_2_e), .F(contador0_6_2_f), .G(contador0_6_2_g),
    .clockpass(contador0_6_2_clockpass));
  not not_1 (not_1_out, clock_1_out);
  CONTADOR0_9 contador0_9_2 (
    .clockglobal(not_1_out), .clockpass(contador0_9_2_clockpass), .G(contador0_9_2_g), .F(contador0_9_2_f),
    .E(contador0_9_2_e), .D(contador0_9_2_d), .C(contador0_9_2_c), .B(contador0_9_2_b), .A(contador0_9_2_a));
  Clock clock_1 (.out(clock_1_out));
endmodule

module CONTADOR0_9 (
  input  clockglobal,
  output clockpass,
  output G,
  output F,
  output E,
  output D,
  output C,
  output B,
  output A
);

  wire contadorcontrol0_9_1_q0j, contadorcontrol0_9_1_q0k, contadorcontrol0_9_1_q1j,
       contadorcontrol0_9_1_q1k, contadorcontrol0_9_1_q2j, contadorcontrol0_9_1_q2k,
       contadorcontrol0_9_1_q3j, contadorcontrol0_9_1_q3k, not_1_out, not_2_out, not_3_out;
  wire [3:0] j_k_ff_4_q;

  not not_1 (not_1_out, clockglobal);
  J_K_Flip_Flop j_k_ff_1 (
    .J(contadorcontrol0_9_1_q3j), .clk(not_1_out), .K(contadorcontrol0_9_1_q3k), .Q(j_k_ff_4_q[3]));  // open: Qn, preset, en, reset
  J_K_Flip_Flop j_k_ff_2 (
    .J(contadorcontrol0_9_1_q2j), .clk(not_1_out), .K(contadorcontrol0_9_1_q2k), .Q(j_k_ff_4_q[2]));  // open: Qn, preset, en, reset
  not not_2 (not_2_out, j_k_ff_4_q[2]);
  not not_3 (not_3_out, j_k_ff_4_q[1]);
  and and_1 (clockpass, j_k_ff_4_q[0], not_3_out, not_2_out, j_k_ff_4_q[3]);
  J_K_Flip_Flop j_k_ff_3 (
    .J(contadorcontrol0_9_1_q1j), .clk(not_1_out), .K(contadorcontrol0_9_1_q1k), .Q(j_k_ff_4_q[1]));  // open: Qn, preset, en, reset
  J_K_Flip_Flop j_k_ff_4 (
    .J(contadorcontrol0_9_1_q0j), .clk(not_1_out), .K(contadorcontrol0_9_1_q0k), .Q(j_k_ff_4_q[0]));  // open: Qn, preset, en, reset
  // display_main main_1: pin names not known; wires that end beside it: G, F, j_k_ff_4_q[0], E, j_k_ff_4_q[1], D, j_k_ff_4_q[2], C, j_k_ff_4_q[3], B, A
  contadorcontrol0_9 contadorcontrol0_9_1 (
    .q3(j_k_ff_4_q[3]), .q2(j_k_ff_4_q[2]), .q1(j_k_ff_4_q[1]), .q0(j_k_ff_4_q[0]),
    .q3j(contadorcontrol0_9_1_q3j), .q3k(contadorcontrol0_9_1_q3k), .q2j(contadorcontrol0_9_1_q2j),
    .q2k(contadorcontrol0_9_1_q2k), .q1j(contadorcontrol0_9_1_q1j), .q1k(contadorcontrol0_9_1_q1k),
    .q0j(contadorcontrol0_9_1_q0j), .q0k(contadorcontrol0_9_1_q0k));
endmodule

module contadorcontrol0_9 (
  input  q3,
  input  q2,
  input  q1,
  input  q0,
  output q3j,
  output q3k,
  output q2j,
  output q2k,
  output q1j,
  output q1k,
  output q0j,
  output q0k
);

  wire not_1_out;

  and and_1 (q3j, q2, q1, q0);
  and and_2 (q2j, q1, q0);
  and and_3 (q2k, q1, q0);
  not not_1 (not_1_out, q3);
  and and_4 (q1j, not_1_out, q0);

  assign q0j = 1'b1;
  assign q0k = 1'b1;
  assign q1k = q0;
  assign q3k = q0;
endmodule

module CONTADORHORA (
  input  clockH,
  output G,
  output F,
  output E,
  output D,
  output C,
  output B,
  output A,
  output g_2,
  output f_2,
  output e_2,
  output d_2,
  output c_2,
  output b_2,
  output a_2
);

  wire corrigidohora2_1_jq0, corrigidohora2_1_jq1, corrigidohora2_1_jq2, corrigidohora2_1_jq3,
       corrigidohora2_1_jq4, corrigidohora2_1_kq0, corrigidohora2_1_kq1, corrigidohora2_1_kq2,
       corrigidohora2_1_kq3, corrigidohora2_1_kq4, j_k_ff_1_q, j_k_ff_2_q, j_k_ff_3_q, j_k_ff_4_q,
       j_k_ff_5_q, leitorcorrigo0_13_1_q0_2, leitorcorrigo0_13_1_q1_2, leitorcorrigo0_13_1_q2_2,
       leitorcorrigo0_13_1_q3_2, main_1_p3, main_1_p5, not_1_out;

  not not_1 (not_1_out, clockH);
  J_K_Flip_Flop j_k_ff_1 (
    .J(corrigidohora2_1_jq4), .clk(not_1_out), .K(corrigidohora2_1_kq4), .Q(j_k_ff_1_q));  // open: Qn, preset, en, reset
  J_K_Flip_Flop j_k_ff_2 (
    .J(corrigidohora2_1_jq3), .clk(not_1_out), .K(corrigidohora2_1_kq3), .Q(j_k_ff_2_q));  // open: Qn, preset, en, reset
  J_K_Flip_Flop j_k_ff_3 (
    .J(corrigidohora2_1_jq2), .clk(not_1_out), .K(corrigidohora2_1_kq2), .Q(j_k_ff_3_q));  // open: Qn, preset, en, reset
  J_K_Flip_Flop j_k_ff_4 (
    .J(corrigidohora2_1_jq1), .clk(not_1_out), .K(corrigidohora2_1_kq1), .Q(j_k_ff_4_q));  // open: Qn, preset, en, reset
  J_K_Flip_Flop j_k_ff_5 (
    .J(corrigidohora2_1_jq0), .clk(not_1_out), .K(corrigidohora2_1_kq0), .Q(j_k_ff_5_q));  // open: Qn, preset, en, reset
  leitorcorrigo0_13 leitorcorrigo0_13_1 (
    .q4(j_k_ff_1_q), .q3(j_k_ff_2_q), .q2(j_k_ff_3_q), .q1(j_k_ff_4_q), .q0(j_k_ff_5_q),
    .Q3_2(leitorcorrigo0_13_1_q3_2), .Q2_2(leitorcorrigo0_13_1_q2_2), .Q1_2(leitorcorrigo0_13_1_q1_2),
    .Q0_2(leitorcorrigo0_13_1_q0_2));
  // display_main main_1: pin names not known; wires that end beside it: G, F, main_1_p3, E, main_1_p5, D, 1'b0, C, 1'b0, B, A
  corrigidohora2 corrigidohora2_1 (
    .q4(j_k_ff_1_q), .q3(j_k_ff_2_q), .q2(j_k_ff_3_q), .q1(j_k_ff_4_q), .q0(j_k_ff_5_q), .S1(main_1_p5),
    .S0(main_1_p3), .jq4(corrigidohora2_1_jq4), .kq4(corrigidohora2_1_kq4), .jq3(corrigidohora2_1_jq3),
    .kq3(corrigidohora2_1_kq3), .jq2(corrigidohora2_1_jq2), .kq2(corrigidohora2_1_kq2),
    .jq1(corrigidohora2_1_jq1), .kq1(corrigidohora2_1_kq1), .jq0(corrigidohora2_1_jq0),
    .kq0(corrigidohora2_1_kq0));
  // display_main main_2: pin names not known; wires that end beside it: leitorcorrigo0_13_1_q3_2, leitorcorrigo0_13_1_q2_2, leitorcorrigo0_13_1_q1_2, leitorcorrigo0_13_1_q0_2, a_2, b_2, c_2, d_2, e_2, f_2, g_2
endmodule

module contadorcontrol0_13 (
  input  q3,
  input  q2,
  input  q1,
  input  q0,
  output q3j,
  output q3k,
  output q2j,
  output q2k,
  output q1j,
  output q1k,
  output q0j,
  output q0k
);

  wire and_4_out, and_5_out, and_6_out, and_7_out, not_1_out, not_2_out;

  and and_1 (q3j, q2, q1, q0);
  and and_2 (q3k, q2, q0);
  and and_3 (q2j, q1, q0);
  and and_4 (and_4_out, q1, q0);
  and and_5 (and_5_out, q3, q0);
  not not_1 (not_1_out, q3);
  and and_6 (and_6_out, not_1_out, q0);
  not not_2 (not_2_out, q2);
  and and_7 (and_7_out, not_2_out, q0);
  or or_1 (q2k, and_4_out, and_5_out);
  or or_2 (q1j, and_6_out, and_7_out);

  assign q0j = 1'b1;
  assign q0k = 1'b1;
  assign q1k = q0;
endmodule

module leitor0_13 (
  input  q3,
  input  q2,
  input  q1,
  input  q0,
  output Q3_2,
  output Q2_2,
  output Q1_2,
  output Q0_2
);

  wire and_3_out, and_4_out, not_1_out, not_2_out, not_3_out, not_4_out;

  not not_1 (not_1_out, q2);
  and and_1 (Q3_2, q3, not_1_out, not_2_out);
  not not_2 (not_2_out, q1);
  not not_3 (not_3_out, q3);
  and and_2 (Q2_2, not_3_out, q2);
  not not_4 (not_4_out, q3);
  and and_3 (and_3_out, not_4_out, q1);
  and and_4 (and_4_out, q3, q2);
  or or_1 (Q1_2, and_3_out, and_4_out);

  assign Q0_2 = q0;
endmodule

module horacontrolador (
  input  q4,
  input  q3,
  input  q2,
  input  q1,
  input  q0,
  output S1,
  output S0,
  output jq4,
  output kq4,
  output jq3,
  output kq3,
  output jq2,
  output kq2,
  output jq1,
  output kq1,
  output jq0,
  output kq0
);

  wire and_5_out, and_6_out, and_8_out, and_9_out, and_10_out, and_12_out, not_1_out, not_2_out, not_3_out,
       not_4_out, not_5_out;

  and and_1 (S1, q4, q2);
  not not_1 (not_1_out, q2);
  and and_2 (jq4, q3, q2, q1, q0);
  and and_3 (kq4, q2, q1, q0);
  not not_2 (not_2_out, q4);
  and and_4 (kq3, q2, q1, q0);
  and and_5 (and_5_out, q1, q0);
  and and_6 (and_6_out, q3, q1);
  and and_7 (kq2, q1, q0);
  not not_3 (not_3_out, q2);
  not not_4 (not_4_out, q4);
  not not_5 (not_5_out, q2);
  or or_1 (kq0, q0, q3);
  and and_8 (and_8_out, q3, q1);
  and and_9 (and_9_out, q3, q2);
  and and_10 (and_10_out, q4, not_1_out);
  and and_11 (jq3, not_2_out, q2, q1, q0);
  or or_2 (jq2, and_5_out, and_6_out);
  and and_12 (and_12_out, q3, not_3_out);
  or or_3 (jq0, not_4_out, not_5_out, q1);
  or or_4 (S0, and_8_out, and_9_out, and_10_out);
  or or_5 (kq1, q0, and_12_out);

  assign jq1 = q0;
endmodule

module corrigidohora (
  input  q4,
  input  q3,
  input  q2,
  input  q1,
  input  q0,
  output S1,
  output S0,
  output jq4,
  output kq4,
  output jq3,
  output kq3,
  output jq2,
  output kq2,
  output jq1,
  output kq1,
  output jq0,
  output kq0
);

  wire and_5_out, and_6_out, and_8_out, and_9_out, and_10_out, and_12_out, not_1_out, not_2_out, not_3_out;

  and and_1 (S1, q4, q2);
  not not_1 (not_1_out, q2);
  and and_2 (jq4, q3, q2, q1, q0);
  and and_3 (kq4, q2, q1, q0);
  not not_2 (not_2_out, q4);
  and and_4 (kq3, q2, q1, q0);
  and and_5 (and_5_out, q1, q0);
  and and_6 (and_6_out, q3, q1);
  and and_7 (kq2, q1, q0);
  not not_3 (not_3_out, q2);
  or or_1 (kq0, q0, q3);
  and and_8 (and_8_out, q3, q1);
  and and_9 (and_9_out, q3, q2);
  and and_10 (and_10_out, q4, not_1_out);
  and and_11 (jq3, not_2_out, q2, q1, q0);
  or or_2 (jq2, and_5_out, and_6_out);
  and and_12 (and_12_out, q3, not_3_out);
  or or_3 (S0, and_8_out, and_9_out, and_10_out);
  or or_4 (kq1, q0, and_12_out);

  assign jq0 = 1'b1;
  assign jq1 = q0;
endmodule

module leitorcorrigo0_13 (
  input  q4,
  input  q3,
  input  q2,
  input  q1,
  input  q0,
  output Q3_2,
  output Q2_2,
  output Q1_2,
  output Q0_2
);

  wire and_1_out, and_2_out, and_3_out, and_4_out, and_5_out, and_6_out, and_7_out, and_8_out, and_9_out,
       not_1_out, not_2_out, not_3_out, not_4_out, not_5_out, not_6_out, not_7_out, not_8_out, not_9_out,
       not_10_out, not_11_out, not_12_out, not_13_out;

  not not_1 (not_1_out, q2);
  not not_2 (not_2_out, q1);
  not not_3 (not_3_out, q2);
  not not_4 (not_4_out, q4);
  not not_5 (not_5_out, q3);
  not not_6 (not_6_out, q2);
  not not_7 (not_7_out, q1);
  not not_8 (not_8_out, q4);
  not not_9 (not_9_out, q3);
  not not_10 (not_10_out, q3);
  not not_11 (not_11_out, q1);
  not not_12 (not_12_out, q2);
  not not_13 (not_13_out, q1);
  and and_1 (and_1_out, q3, not_1_out, not_2_out);
  and and_2 (and_2_out, q4, not_3_out, q1);
  and and_3 (and_3_out, not_4_out, not_5_out, q2);
  and and_4 (and_4_out, q3, q2, q1);
  and and_5 (and_5_out, q4, not_6_out, not_7_out);
  and and_6 (and_6_out, not_8_out, not_9_out, q1);
  and and_7 (and_7_out, not_10_out, q2, q1);
  and and_8 (and_8_out, q3, q2, not_11_out);
  and and_9 (and_9_out, q4, not_12_out, not_13_out);
  or or_1 (Q3_2, and_1_out, and_2_out);
  or or_2 (Q2_2, and_3_out, and_4_out, and_5_out);
  or or_3 (Q1_2, and_6_out, and_7_out, and_8_out, and_9_out);

  assign Q0_2 = q0;
endmodule

module corrigidohora2 (
  input  q4,
  input  q3,
  input  q2,
  input  q1,
  input  q0,
  output S1,
  output S0,
  output jq4,
  output kq4,
  output jq3,
  output kq3,
  output jq2,
  output kq2,
  output jq1,
  output kq1,
  output jq0,
  output kq0
);

  wire and_5_out, and_6_out, and_7_out, and_9_out, and_10_out, and_11_out, and_13_out, and_14_out, not_1_out,
       not_2_out, not_3_out, not_4_out, not_5_out;

  and and_1 (S1, q4, q2);
  not not_1 (not_1_out, q2);
  and and_2 (jq4, q3, q2, q1, q0);
  and and_3 (kq4, q2, q1, q0);
  not not_2 (not_2_out, q4);
  and and_4 (kq3, q2, q1, q0);
  and and_5 (and_5_out, q1, q0);
  and and_6 (and_6_out, q3, q2, q1);
  and and_7 (and_7_out, q4, q3, q1);
  and and_8 (kq2, q1, q0);
  not not_3 (not_3_out, q2);
  not not_4 (not_4_out, q1);
  not not_5 (not_5_out, q2);
  or or_1 (kq0, q0, q3);
  and and_9 (and_9_out, q3, q1);
  and and_10 (and_10_out, q3, q2);
  and and_11 (and_11_out, q4, not_1_out);
  and and_12 (jq3, not_2_out, q2, q1, q0);
  or or_2 (jq2, and_5_out, and_6_out, and_7_out);
  and and_13 (and_13_out, q3, not_3_out, not_4_out);
  and and_14 (and_14_out, q4, q3, not_5_out);
  or or_3 (S0, and_9_out, and_10_out, and_11_out);
  or or_4 (kq1, q0, and_13_out, and_14_out);

  assign jq0 = 1'b1;
  assign jq1 = q0;
endmodule

module control0_6 (
  input  q2,
  input  q1,
  input  q0,
  output jq2,
  output kq2,
  output jq1,
  output kq1,
  output jq0,
  output kq0
);

  wire and_1_out, and_2_out, and_3_out, and_4_out, not_1_out, not_2_out, not_3_out;

  and and_1 (and_1_out, q1, q0);
  and and_2 (and_2_out, q2, q0);
  or or_1 (kq2, q0, q1);
  not not_1 (not_1_out, q2);
  or or_2 (kq1, q0, q2);
  not not_2 (not_2_out, q2);
  not not_3 (not_3_out, q1);
  or or_3 (jq2, and_1_out, and_2_out);
  and and_3 (and_3_out, not_1_out, q0);
  and and_4 (and_4_out, q2, q1);
  or or_4 (jq0, not_2_out, not_3_out, q0);
  or or_5 (jq1, and_3_out, and_4_out);

  assign kq0 = 1'b1;
endmodule

module CONTADOR0_6 (
  input  clock,
  output A,
  output B,
  output C,
  output D,
  output E,
  output F,
  output G,
  output clockpass
);

  wire control0_6_1_jq0, control0_6_1_jq1, control0_6_1_jq2, control0_6_1_kq0, control0_6_1_kq1,
       control0_6_1_kq2, j_k_ff_1_q, j_k_ff_2_q, j_k_ff_3_q, not_1_out, not_2_out;

  not not_1 (not_1_out, clock);
  J_K_Flip_Flop j_k_ff_1 (
    .J(control0_6_1_jq2), .clk(not_1_out), .K(control0_6_1_kq2), .Q(j_k_ff_1_q));  // open: Qn, preset, en, reset
  J_K_Flip_Flop j_k_ff_2 (
    .J(control0_6_1_jq1), .clk(not_1_out), .K(control0_6_1_kq1), .Q(j_k_ff_2_q));  // open: Qn, preset, en, reset
  not not_2 (not_2_out, j_k_ff_2_q);
  and and_1 (clockpass, j_k_ff_1_q, not_2_out, j_k_ff_3_q);
  J_K_Flip_Flop j_k_ff_3 (
    .J(control0_6_1_jq0), .clk(not_1_out), .K(control0_6_1_kq0), .Q(j_k_ff_3_q));  // open: Qn, preset, en, reset
  control0_6 control0_6_1 (
    .q2(j_k_ff_1_q), .q1(j_k_ff_2_q), .q0(j_k_ff_3_q), .jq2(control0_6_1_jq2), .kq2(control0_6_1_kq2),
    .jq1(control0_6_1_jq1), .kq1(control0_6_1_kq1), .jq0(control0_6_1_jq0), .kq0(control0_6_1_kq0));
  // display_main main_1: pin names not known; wires that end beside it: 1'b0, j_k_ff_1_q, j_k_ff_2_q, j_k_ff_3_q, A, B, C, D, E, F, G
endmodule
