// Logisim project Relogio.circ as structural Verilog: 13 circuits, main circuit main
module main (
);

  wire clock_1_out, contador_4_1_clock_2, contador_6_1_clock_2, contador_6_2_clock_2, contador_6_2_glitch,
       contador_9_1_clock_2, contador_9_2_clock_2, n0_9_1_a, n0_9_1_b, n0_9_1_c, n0_9_1_d, n0_9_1_e,
       n0_9_1_f, n0_9_1_g, n0_9_2_a, n0_9_2_b, n0_9_2_c, n0_9_2_d, n0_9_2_e, n0_9_2_f, n0_9_2_g, n0_9_3_a,
       n0_9_3_b, n0_9_3_c, n0_9_3_d, n0_9_3_e, n0_9_3_f, n0_9_3_g, n0_9_4_a, n0_9_4_b, n0_9_4_c, n0_9_4_d,
       n0_9_4_e, n0_9_4_f, n0_9_4_g, n0_9_5_a, n0_9_5_b, n0_9_5_c, n0_9_5_d, n0_9_5_e, n0_9_5_f, n0_9_5_g,
       n0_9_6_a, n0_9_6_b, n0_9_6_c, n0_9_6_d, n0_9_6_e, n0_9_6_f, n0_9_6_g;
  wire [3:0] contador_2_1_out_3, contador_4_1_out_3, contador_6_1_out_3, contador_6_2_out_3,
       contador_9_1_out_3, contador_9_2_out_3;

  Clock clock_1 (.out(clock_1_out));
  CONTADOR_2 contador_2_1 (.CLOCK(contador_4_1_clock_2), .out_3(contador_2_1_out_3));  // open: RESET, CLOCK_2, GLITCH
  CONTADOR_4 contador_4_1 (
    .CLOCK(contador_6_1_clock_2), .out_3(contador_4_1_out_3), .CLOCK_2(contador_4_1_clock_2));  // open: RESET, GLITCH
  CONTADOR_6 contador_6_1 (
    .CLOCK(contador_9_1_clock_2), .out_3(contador_6_1_out_3), .CLOCK_2(contador_6_1_clock_2));  // open: RESET, GLITCH
  CONTADOR_9 contador_9_1 (
    .CLOCK(contador_6_2_clock_2), .out_3(contador_9_1_out_3), .CLOCK_2(contador_9_1_clock_2));  // open: RESET, GLITCH
  CONTADOR_6 contador_6_2 (
    .CLOCK(contador_9_2_clock_2), .out_3(contador_6_2_out_3), .CLOCK_2(contador_6_2_clock_2),
    .GLITCH(contador_6_2_glitch));  // open: RESET
  CONTADOR_9 contador_9_2 (
    .CLOCK(clock_1_out), .RESET(contador_6_2_glitch), .out_3(contador_9_2_out_3),
    .CLOCK_2(contador_9_2_clock_2));  // open: GLITCH
  _0_9 u_0_9_1 (
    .Numero_Em_Binario(contador_2_1_out_3), .A(n0_9_1_a), .B(n0_9_1_b), .C(n0_9_1_c), .D(n0_9_1_d),
    .E(n0_9_1_e), .F(n0_9_1_f), .G(n0_9_1_g));  // open: H
  _0_9 u_0_9_2 (
    .Numero_Em_Binario(contador_4_1_out_3), .A(n0_9_2_a), .B(n0_9_2_b), .C(n0_9_2_c), .D(n0_9_2_d),
    .E(n0_9_2_e), .F(n0_9_2_f), .G(n0_9_2_g));  // open: H
  _0_9 u_0_9_3 (
    .Numero_Em_Binario(contador_6_1_out_3), .A(n0_9_3_a), .B(n0_9_3_b), .C(n0_9_3_c), .D(n0_9_3_d),
    .E(n0_9_3_e), .F(n0_9_3_f), .G(n0_9_3_g));  // open: H
  _0_9 u_0_9_4 (
    .Numero_Em_Binario(contador_9_1_out_3), .A(n0_9_4_a), .B(n0_9_4_b), .C(n0_9_4_c), .D(n0_9_4_d),
    .E(n0_9_4_e), .F(n0_9_4_f), .G(n0_9_4_g));  // open: H
  _0_9 u_0_9_5 (
    .Numero_Em_Binario(contador_6_2_out_3), .A(n0_9_5_a), .B(n0_9_5_b), .C(n0_9_5_c), .D(n0_9_5_d),
    .E(n0_9_5_e), .F(n0_9_5_f), .G(n0_9_5_g));  // open: H
  _0_9 u_0_9_6 (
    .Numero_Em_Binario(contador_9_2_out_3), .A(n0_9_6_a), .B(n0_9_6_b), .C(n0_9_6_c), .D(n0_9_6_d),
    .E(n0_9_6_e), .F(n0_9_6_f), .G(n0_9_6_g));  // open: H
  _7_Segment_Display u_7_segment_display_1 (
    .g(n0_9_1_d), .f(n0_9_1_c), .a(n0_9_1_b), .b(n0_9_1_a), .e(n0_9_1_e), .d(n0_9_1_f), .c(n0_9_1_g));  // open: dp
  _7_Segment_Display u_7_segment_display_2 (
    .g(n0_9_3_d), .f(n0_9_3_c), .a(n0_9_3_b), .b(n0_9_3_a), .e(n0_9_3_e), .d(n0_9_3_f), .c(n0_9_3_g));  // open: dp
  _7_Segment_Display u_7_segment_display_3 (
    .g(n0_9_2_d), .f(n0_9_2_c), .a(n0_9_2_b), .b(n0_9_2_a), .e(n0_9_2_e), .d(n0_9_2_f), .c(n0_9_2_g));  // open: dp
  _7_Segment_Display u_7_segment_display_4 (
    .g(n0_9_5_d), .f(n0_9_5_c), .a(n0_9_5_b), .b(n0_9_5_a), .e(n0_9_5_e), .d(n0_9_5_f), .c(n0_9_5_g));  // open: dp
  _7_Segment_Display u_7_segment_display_5 (
    .g(n0_9_4_d), .f(n0_9_4_c), .a(n0_9_4_b), .b(n0_9_4_a), .e(n0_9_4_e), .d(n0_9_4_f), .c(n0_9_4_g));  // open: dp
  _7_Segment_Display u_7_segment_display_6 (
    .g(n0_9_6_d), .f(n0_9_6_c), .a(n0_9_6_b), .b(n0_9_6_a), .e(n0_9_6_e), .d(n0_9_6_f), .c(n0_9_6_g));  // open: dp
endmodule

module _0_9 (
  input  [3:0] Numero_Em_Binario,
  output A,
  output B,
  output C,
  output D,
  output E,
  output F,
  output G,
  output H
);

  SAIDA_A saida_a_1 (.in_1(Numero_Em_Binario), .s(A));
  SAIDA_B saida_b_1 (.in_1(Numero_Em_Binario), .s(B));
  SAIDA_C saida_c_1 (.in_1(Numero_Em_Binario), .s(C));
  SAIDA_D saida_d_1 (.in_1(Numero_Em_Binario), .s(D));
  SAIDA_E saida_e_1 (.in_1(Numero_Em_Binario), .s(E));
  SAIDA_F saida_f_1 (.in_1(Numero_Em_Binario), .s(F));
  SAIDA_G saida_g_1 (.in_1(Numero_Em_Binario), .s(G));

  assign H = 1'b0;
endmodule

module SAIDA_A (
  input  [3:0] in_1,
  output s
);

  wire and_1_out, and_2_out, not_1_out, not_2_out, not_3_out;

  not not_1 (not_1_out, in_1[1]);
  not not_2 (not_2_out, in_1[0]);
  not not_3 (not_3_out, in_1[2]);
  and and_1 (and_1_out, not_1_out, not_2_out);
  and and_2 (and_2_out, in_1[1], in_1[0]);
  or or_1 (s, not_3_out, and_1_out, and_2_out);
endmodule

module SAIDA_B (
  input  [3:0] in_1,
  output s
);

  wire and_1_out, and_2_out, not_1_out, not_2_out;

  not not_1 (not_1_out, in_1[2]);
  and and_1 (and_1_out, not_1_out, not_2_out);
  not not_2 (not_2_out, in_1[0]);
  and and_2 (and_2_out, in_1[2], in_1[0]);
  or or_1 (s, and_1_out, in_1[1], and_2_out, in_1[3]);
endmodule

module SAIDA_C (
  input  [3:0] in_1,
  output s
);

  wire and_1_out, and_2_out, and_3_out, not_1_out, not_2_out, not_3_out, not_4_out;

  not not_1 (not_1_out, in_1[1]);
  and and_1 (and_1_out, not_1_out, not_2_out);
  not not_2 (not_2_out, in_1[0]);
  and and_2 (and_2_out, in_1[2], not_3_out);
  not not_3 (not_3_out, in_1[1]);
  and and_3 (and_3_out, in_1[2], not_4_out);
  not not_4 (not_4_out, in_1[0]);
  or or_1 (s, and_1_out, and_2_out, and_3_out, in_1[3]);
endmodule

module SAIDA_E (
  input  [3:0] in_1,
  output s
);

  wire and_1_out, and_2_out, not_1_out, not_2_out, not_3_out;

  not not_1 (not_1_out, in_1[2]);
  and and_1 (and_1_out, not_1_out, not_2_out);
  not not_2 (not_2_out, in_1[0]);
  and and_2 (and_2_out, in_1[1], not_3_out);
  not not_3 (not_3_out, in_1[0]);
  or or_1 (s, and_1_out, and_2_out);
endmodule

module SAIDA_D (
  input  [3:0] in_1,
  output s
);

  wire and_1_out, and_2_out, and_3_out, not_1_out, not_2_out, not_3_out;

  not not_1 (not_1_out, in_1[2]);
  and and_1 (and_1_out, not_1_out, in_1[1]);
  and and_2 (and_2_out, in_1[1], not_2_out);
  not not_2 (not_2_out, in_1[0]);
  and and_3 (and_3_out, in_1[2], not_3_out);
  not not_3 (not_3_out, in_1[1]);
  or or_1 (s, and_1_out, and_2_out, and_3_out, in_1[3]);
endmodule

module SAIDA_F (
  input  [3:0] in_1,
  output s
);

  wire and_1_out, and_2_out, and_3_out, and_4_out, not_1_out, not_2_out, not_3_out, not_4_out, not_5_out;

  not not_1 (not_1_out, in_1[2]);
  and and_1 (and_1_out, not_1_out, not_2_out);
  not not_2 (not_2_out, in_1[0]);
  not not_3 (not_3_out, in_1[2]);
  and and_2 (and_2_out, not_3_out, in_1[1]);
  and and_3 (and_3_out, in_1[1], not_4_out);
  not not_4 (not_4_out, in_1[0]);
  not not_5 (not_5_out, in_1[1]);
  and and_4 (and_4_out, in_1[2], not_5_out, in_1[0]);
  or or_1 (s, and_1_out, and_2_out, and_3_out, and_4_out);
endmodule

module SAIDA_G (
  input  [3:0] in_1,
  output s
);

  wire not_1_out;

  not not_1 (not_1_out, in_1[1]);
  or or_1 (s, not_1_out, in_1[0], in_1[2]);
endmodule

// 9
module CONTADOR_9 (
  input  CLOCK,
  input  RESET,
  output [3:0] out_3,
  output CLOCK_2,
  output GLITCH
);

  wire or_1_out, t_ff_1_qn, t_ff_2_qn, t_ff_3_qn;

  T_Flip_Flop t_ff_1 (.clk(CLOCK), .T(1'b1), .Q(out_3[0]), .Qn(t_ff_1_qn), .preset(1'b0), .reset(or_1_out), .en(1'b1));
  T_Flip_Flop t_ff_2 (
    .clk(t_ff_1_qn), .T(1'b1), .Q(out_3[1]), .Qn(t_ff_2_qn), .preset(1'b0), .reset(or_1_out), .en(1'b1));
  T_Flip_Flop t_ff_3 (
    .clk(t_ff_2_qn), .T(1'b1), .Q(out_3[2]), .Qn(t_ff_3_qn), .preset(1'b0), .reset(or_1_out), .en(1'b1));
  or or_1 (or_1_out, RESET, CLOCK_2);
  T_Flip_Flop t_ff_4 (.clk(t_ff_3_qn), .T(1'b1), .Q(out_3[3]), .preset(1'b0), .reset(or_1_out), .en(1'b1));  // open: Qn
  and and_1 (CLOCK_2, ~out_3[0], out_3[1], ~out_3[2], out_3[3]);  // AND_Gate

  assign GLITCH = CLOCK_2;
endmodule

// 5
module CONTADOR_6 (
  input  CLOCK,
  input  RESET,
  output [3:0] out_3,
  output CLOCK_2,
  output GLITCH
);

  wire or_1_out, t_ff_1_qn, t_ff_2_qn, t_ff_3_qn;

  T_Flip_Flop t_ff_1 (.clk(CLOCK), .T(1'b1), .Q(out_3[0]), .Qn(t_ff_1_qn), .preset(1'b0), .reset(or_1_out), .en(1'b1));
  T_Flip_Flop t_ff_2 (
    .clk(t_ff_1_qn), .T(1'b1), .Q(out_3[1]), .Qn(t_ff_2_qn), .preset(1'b0), .reset(or_1_out), .en(1'b1));
  or or_1 (or_1_out, RESET, GLITCH);
  T_Flip_Flop t_ff_3 (
    .clk(t_ff_2_qn), .T(1'b1), .Q(out_3[2]), .Qn(t_ff_3_qn), .preset(1'b0), .reset(or_1_out), .en(1'b1));
  T_Flip_Flop t_ff_4 (
    .clk(t_ff_3_qn), .T(1'b1), .Q(out_3[3]), .Qn(CLOCK_2), .preset(1'b0), .reset(or_1_out), .en(1'b1));
  and and_1 (GLITCH, ~out_3[0], out_3[1], out_3[2], ~out_3[3]);  // AND_Gate
endmodule

// 2
module CONTADOR_2 (
  input  CLOCK,
  input  RESET,
  output [3:0] out_3,
  output CLOCK_2,
  output GLITCH
);

  wire or_1_out, t_ff_1_qn;

  T_Flip_Flop t_ff_1 (.clk(CLOCK), .T(1'b1), .Q(out_3[0]), .Qn(t_ff_1_qn), .preset(1'b0), .reset(or_1_out), .en(1'b1));
  T_Flip_Flop t_ff_2 (
    .clk(t_ff_1_qn), .T(1'b1), .Q(out_3[1]), .Qn(CLOCK_2), .preset(1'b0), .reset(or_1_out), .en(1'b1));
  or or_1 (or_1_out, RESET, GLITCH);
  and and_1 (GLITCH, out_3[0], out_3[1], ~1'b0, ~1'b0);  // AND_Gate

  assign out_3[3:2] = 2'b00;
endmodule

// 4
module CONTADOR_4 (
  input  CLOCK,
  input  RESET,
  output [3:0] out_3,
  output CLOCK_2,
  output GLITCH
);

  wire or_1_out, t_ff_1_qn, t_ff_2_qn;

  T_Flip_Flop t_ff_1 (.clk(CLOCK), .T(1'b1), .Q(out_3[0]), .Qn(t_ff_1_qn), .preset(1'b0), .reset(or_1_out), .en(1'b1));
  T_Flip_Flop t_ff_2 (
    .clk(t_ff_1_qn), .T(1'b1), .Q(out_3[1]), .Qn(t_ff_2_qn), .preset(1'b0), .reset(or_1_out), .en(1'b1));
  or or_1 (or_1_out, RESET, GLITCH);
  T_Flip_Flop t_ff_3 (
    .clk(t_ff_2_qn), .T(1'b1), .Q(out_3[2]), .Qn(CLOCK_2), .preset(1'b0), .reset(or_1_out), .en(1'b1));
  and and_1 (GLITCH, out_3[0], ~out_3[1], out_3[2], ~1'b0);  // AND_Gate

  assign out_3[3] = 1'b0;
endmodule
