// Logisim project ULA.circ as structural Verilog: 2 circuits, main circuit main
module main (
  input  [3:0] OP,
  input  [7:0] A,
  input  [7:0] B,
  output [7:0] SAIDA
);

  wire and_13_out, not_1_out, not_2_out, not_3_out, not_4_out, not_5_out, not_6_out, not_7_out, not_8_out,
       not_9_out, not_10_out, not_11_out, not_12_out, not_13_out, not_14_out, not_15_out, not_16_out,
       not_17_out, not_18_out, not_19_out, not_21_out, not_22_out, not_23_out, not_24_out, not_25_out;
  wire [1:0] or_6_out;
  wire [7:0] and_1_out, and_4_out, and_6_out, and_8_out, and_12_out, and_15_out, and_16_out, main_1_s0,
       multiplexer_1_out, nor_1_out, not_20_out, or_1_out, or_2_out, or_3_out, or_4_out, or_7_out, xor_1_out;
  wire [7:7] and_2_out, and_3_out, and_5_out, and_7_out, and_9_out, and_10_out, and_11_out, and_14_out,
       and_17_out;

  not not_1 (not_1_out, OP[3]);
  not not_2 (not_2_out, OP[1]);
  assign and_1_out = A & B;  // AND_Gate and_1, 8 bits wide
  assign or_1_out = A | B;  // OR_Gate or_1, 8 bits wide
  assign xor_1_out = A ^ B;  // XOR_Gate xor_1, 8 bits wide
  not not_3 (not_3_out, OP[1]);
  not not_4 (not_4_out, OP[0]);
  not not_5 (not_5_out, OP[2]);
  not not_6 (not_6_out, OP[3]);
  and and_2 (and_2_out[7], not_1_out, not_2_out, not_5_out, not_4_out);
  and and_3 (and_3_out[7], not_6_out, not_3_out, not_7_out, OP[0]);
  assign or_2_out = {8{and_2_out[7]}} | {8{and_7_out[7]}};  // OR_Gate or_2, 8 bits wide
  assign and_4_out = or_2_out & nor_1_out & and_1_out;  // AND_Gate and_4, 8 bits wide
  not not_7 (not_7_out, OP[2]);
  not not_8 (not_8_out, OP[2]);
  not not_9 (not_9_out, OP[3]);
  and and_5 (and_5_out[7], not_9_out, OP[1], not_8_out, OP[0]);
  assign or_3_out = {8{and_3_out[7]}} | {8{and_10_out[7]}};  // OR_Gate or_3, 8 bits wide
  assign or_4_out = {8{and_5_out[7]}} | {8{and_9_out[7]}};  // OR_Gate or_4, 8 bits wide
  assign and_6_out = or_3_out & nor_1_out & or_1_out;  // AND_Gate and_6, 8 bits wide
  not not_10 (not_10_out, OP[3]);
  not not_11 (not_11_out, OP[3]);
  not not_12 (not_12_out, OP[1]);
  and and_7 (and_7_out[7], not_11_out, not_12_out, OP[2], OP[0]);
  assign nor_1_out = ~({8{and_7_out[7]}} | {8{and_10_out[7]}} | {8{and_9_out[7]}} | {8{and_11_out[7]}});  // NOR_Gate nor_1, 8 bits wide
  assign and_8_out = or_4_out & nor_1_out & xor_1_out;  // AND_Gate and_8, 8 bits wide
  not not_13 (not_13_out, OP[2]);
  not not_14 (not_14_out, OP[3]);
  not not_15 (not_15_out, OP[0]);
  and and_9 (and_9_out[7], not_14_out, OP[1], OP[2], not_17_out);
  and and_10 (and_10_out[7], not_10_out, OP[1], not_13_out, not_15_out);
  Multiplexer #(.select(2), .width(8), .enable("false")) multiplexer_1 (
    .in0(A), .in1(xor_1_out), .in2(or_1_out), .in3(and_1_out), .out(multiplexer_1_out), .sel(or_6_out));
  not not_16 (not_16_out, OP[3]);
  not not_17 (not_17_out, OP[0]);
  not not_18 (not_18_out, OP[1]);
  not not_19 (not_19_out, OP[0]);
  and and_11 (and_11_out[7], not_16_out, not_18_out, OP[2], not_19_out);
  assign and_12_out = ~nor_1_out & not_20_out;  // AND_Gate and_12, 8 bits wide
  assign not_20_out = ~multiplexer_1_out;  // NOT_Gate not_20, 8 bits wide
  altodesempenhonewCARRYcorecto_main main_1 (
    .B(B), .A(A), .s7(main_1_s0[7]), .s6(main_1_s0[6]), .s5(main_1_s0[5]), .s4(main_1_s0[4]),
    .s3(main_1_s0[3]), .s2(main_1_s0[2]), .s1(main_1_s0[1]), .s0(main_1_s0[0]), .C0(OP[3]));  // open: c7
  not not_21 (not_21_out, OP[2]);
  or or_5 (or_6_out[1], not_21_out, OP[0]);
  or or_6 (or_6_out[0], OP[0], and_13_out);
  not not_22 (not_22_out, OP[3]);
  and and_13 (and_13_out, OP[1], OP[2]);
  and and_14 (and_14_out[7], not_22_out, OP[1], OP[2], OP[0]);
  assign and_15_out = {8{and_14_out[7]}} & main_1_s0;  // AND_Gate and_15, 8 bits wide
  assign and_16_out = {8{and_17_out[7]}} & main_1_s0;  // AND_Gate and_16, 8 bits wide
  not not_23 (not_23_out, OP[1]);
  and and_17 (and_17_out[7], OP[3], not_23_out, not_24_out, not_25_out);
  assign or_7_out = and_15_out | and_16_out;  // OR_Gate or_7, 8 bits wide
  not not_24 (not_24_out, OP[2]);
  not not_25 (not_25_out, OP[0]);
  assign SAIDA = and_4_out | and_6_out | or_7_out | and_8_out | and_12_out;  // OR_Gate or_8, 8 bits wide

  // Notes on the sheet:
  //   AND
  //   OR
  //   XOR
  //   NAND
  //   NOR
  //   XNOR
  //   NOT
  //   SUM
  //   SUB
endmodule

module \interface  (
  input  [3:0] OP,
  input  [7:0] A,
  input  [7:0] B
);

  wire n0_9_1_a, n0_9_1_b, n0_9_1_c, n0_9_1_d, n0_9_1_e, n0_9_1_f, n0_9_1_g, n0_9_2_a, n0_9_2_b, n0_9_2_c,
       n0_9_2_d, n0_9_2_e, n0_9_2_f, n0_9_2_g, n0_9_3_a, n0_9_3_b, n0_9_3_c, n0_9_3_d, n0_9_3_e, n0_9_3_f,
       n0_9_3_g, n0_9_4_a, n0_9_4_b, n0_9_4_c, n0_9_4_d, n0_9_4_e, n0_9_4_f, n0_9_4_g, n0_9_5_a, n0_9_5_b,
       n0_9_5_c, n0_9_5_d, n0_9_5_e, n0_9_5_f, n0_9_5_g, n0_9_6_a, n0_9_6_b, n0_9_6_c, n0_9_6_d, n0_9_6_e,
       n0_9_6_f, n0_9_6_g;
  wire [3:0] main_1_saida, main_1_saida_2;

  _0_9 u_0_9_1 (
    .Numero_Em_Binario(B[7:4]), .A(n0_9_1_a), .B(n0_9_1_b), .C(n0_9_1_c), .D(n0_9_1_d), .E(n0_9_1_e),
    .F(n0_9_1_f), .G(n0_9_1_g));  // open: H
  _0_9 u_0_9_2 (
    .Numero_Em_Binario(B[3:0]), .A(n0_9_2_a), .B(n0_9_2_b), .C(n0_9_2_c), .D(n0_9_2_d), .E(n0_9_2_e),
    .F(n0_9_2_f), .G(n0_9_2_g));  // open: H
  _0_9 u_0_9_3 (
    .Numero_Em_Binario(A[3:0]), .A(n0_9_3_a), .B(n0_9_3_b), .C(n0_9_3_c), .D(n0_9_3_d), .E(n0_9_3_e),
    .F(n0_9_3_f), .G(n0_9_3_g));  // open: H
  _0_9 u_0_9_4 (
    .Numero_Em_Binario(A[7:4]), .A(n0_9_4_a), .B(n0_9_4_b), .C(n0_9_4_c), .D(n0_9_4_d), .E(n0_9_4_e),
    .F(n0_9_4_f), .G(n0_9_4_g));  // open: H
  _0_9 u_0_9_5 (
    .Numero_Em_Binario(main_1_saida_2), .A(n0_9_5_a), .B(n0_9_5_b), .C(n0_9_5_c), .D(n0_9_5_d), .E(n0_9_5_e),
    .F(n0_9_5_f), .G(n0_9_5_g));  // open: H
  _0_9 u_0_9_6 (
    .Numero_Em_Binario(main_1_saida), .A(n0_9_6_a), .B(n0_9_6_b), .C(n0_9_6_c), .D(n0_9_6_d), .E(n0_9_6_e),
    .F(n0_9_6_f), .G(n0_9_6_g));  // open: H
  _7_Segment_Display u_7_segment_display_1 (
    .g(n0_9_1_d), .f(n0_9_1_c), .a(n0_9_1_b), .b(n0_9_1_a), .e(n0_9_1_e), .d(n0_9_1_f), .c(n0_9_1_g));  // open: dp
  _7_Segment_Display u_7_segment_display_2 (
    .g(n0_9_3_d), .f(n0_9_3_c), .a(n0_9_3_b), .b(n0_9_3_a), .e(n0_9_3_e), .d(n0_9_3_f), .c(n0_9_3_g));  // open: dp
  _7_Segment_Display u_7_segment_display_3 (
    .g(n0_9_2_d), .f(n0_9_2_c), .a(n0_9_2_b), .b(n0_9_2_a), .e(n0_9_2_e), .d(n0_9_2_f), .c(n0_9_2_g));  // open: dp
  _7_Segment_Display u_7_segment_display_4 (
    .g(n0_9_4_d), .f(n0_9_4_c), .a(n0_9_4_b), .b(n0_9_4_a), .e(n0_9_4_e), .d(n0_9_4_f), .c(n0_9_4_g));  // open: dp
  _7_Segment_Display u_7_segment_display_5 (
    .g(n0_9_5_d), .f(n0_9_5_c), .a(n0_9_5_b), .b(n0_9_5_a), .e(n0_9_5_e), .d(n0_9_5_f), .c(n0_9_5_g));  // open: dp
  _7_Segment_Display u_7_segment_display_6 (
    .g(n0_9_6_d), .f(n0_9_6_c), .a(n0_9_6_b), .b(n0_9_6_a), .e(n0_9_6_e), .d(n0_9_6_f), .c(n0_9_6_g));  // open: dp
  main main_1 (.A(A), .B(B), .SAIDA({main_1_saida_2, main_1_saida}), .OP(OP));
endmodule
