// Logisim project somador 4bits.circ as structural Verilog: 1 circuit, main circuit somador4bits
module somador4bits (
  input  b3,
  input  a3,
  input  b2,
  input  a2,
  input  b1,
  input  a1,
  input  b0,
  input  a0,
  input  entrada_0,
  output cout,
  output s3,
  output s2,
  output s1,
  output s0
);

  wire somador1bit_2_co, somador1bit_3_co, somador1bit_4_co;

  somador1bit somador1bit_1 (.C_in(somador1bit_2_co), .Entrada_bit_1(a3), .Entrada_bit_2(b3), .Co(cout), .P(s3));
  somador1bit somador1bit_2 (
    .C_in(somador1bit_3_co), .Entrada_bit_1(a2), .Entrada_bit_2(b2), .Co(somador1bit_2_co), .P(s2));
  somador1bit somador1bit_3 (
    .C_in(somador1bit_4_co), .Entrada_bit_1(a1), .Entrada_bit_2(b1), .Co(somador1bit_3_co), .P(s1));
  somador1bit somador1bit_4 (.C_in(entrada_0), .Entrada_bit_1(a0), .Entrada_bit_2(b0), .Co(somador1bit_4_co), .P(s0));
endmodule
