// Logisim project ULA.circ as structural Verilog: 1 circuit, main circuit main
module main (
  input  [2:0] OP,
  input  [7:0] A,
  input  [7:0] B,
  output [7:0] out_4
);

  wire and_13_out, not_1_out, not_2_out, not_3_out, not_4_out, not_5_out, not_6_out, not_7_out, not_8_out,
       not_9_out, not_11_out, not_12_out, not_13_out, not_14_out;
  wire [1:0] or_7_out;
  wire [7:0] and_3_out, and_4_out, and_6_out, and_8_out, and_12_out, multiplexer_1_out, not_10_out, or_1_out,
       or_2_out, or_3_out, or_4_out, or_5_out, xor_1_out;
  wire [7:7] and_1_out, and_2_out, and_5_out, and_7_out, and_9_out, and_10_out, and_11_out;

  not not_1 (not_1_out, OP[0]);
  not not_2 (not_2_out, OP[1]);
  not not_3 (not_3_out, OP[0]);
  not not_4 (not_4_out, OP[2]);
  not not_5 (not_5_out, OP[1]);
  and and_1 (and_1_out[7], not_3_out, not_2_out, OP[2]);
  and and_2 (and_2_out[7], not_1_out, not_5_out, not_4_out);
  assign or_1_out = {8{and_2_out[7]}} | {8{and_7_out[7]}};  // OR_Gate or_1, 8 bits wide
  assign and_3_out = or_1_out & and_4_out;  // AND_Gate and_3, 8 bits wide
  assign and_4_out = A & B;  // AND_Gate and_4, 8 bits wide
  assign or_2_out = A | B;  // OR_Gate or_2, 8 bits wide
  assign xor_1_out = A ^ B;  // XOR_Gate xor_1, 8 bits wide
  not not_6 (not_6_out, OP[1]);
  and and_5 (and_5_out[7], OP[0], not_6_out, OP[2]);
  assign or_3_out = {8{and_1_out[7]}} | {8{and_10_out[7]}};  // OR_Gate or_3, 8 bits wide
  assign or_4_out = {8{and_5_out[7]}} | {8{and_9_out[7]}};  // OR_Gate or_4, 8 bits wide
  assign and_6_out = or_3_out & or_2_out;  // AND_Gate and_6, 8 bits wide
  not not_7 (not_7_out, OP[0]);
  and and_7 (and_7_out[7], not_7_out, OP[1], OP[2]);
  assign or_5_out = {8{and_7_out[7]}} | {8{and_10_out[7]}} | {8{and_9_out[7]}} | {8{and_11_out[7]}};  // OR_Gate or_5, 8 bits wide
  assign and_8_out = or_4_out & xor_1_out;  // AND_Gate and_8, 8 bits wide
  not not_8 (not_8_out, OP[2]);
  not not_9 (not_9_out, OP[1]);
  and and_9 (and_9_out[7], OP[0], OP[1], not_13_out);
  and and_10 (and_10_out[7], OP[0], not_9_out, not_8_out);
  Multiplexer #(.select(2), .width(8), .enable("false")) multiplexer_1 (
    .in0(A), .in1(and_8_out), .in2(and_6_out), .in3(and_3_out), .out(multiplexer_1_out), .sel(or_7_out));
  assign not_10_out = ~multiplexer_1_out;  // NOT_Gate not_10, 8 bits wide
  not not_11 (not_11_out, OP[0]);
  not not_12 (not_12_out, OP[2]);
  not not_13 (not_13_out, OP[2]);
  and and_11 (and_11_out[7], not_11_out, OP[1], not_12_out);
  assign and_12_out = or_5_out & not_10_out;  // AND_Gate and_12, 8 bits wide
  not not_14 (not_14_out, OP[1]);
  or or_6 (or_7_out[1], not_14_out, OP[2]);
  or or_7 (or_7_out[0], OP[2], and_13_out);
  and and_13 (and_13_out, OP[0], OP[1]);
  assign out_4 = and_3_out | and_6_out | and_8_out | and_12_out;  // OR_Gate or_8, 8 bits wide

  // Notes on the sheet:
  //   OR
  //   AND
  //   XOR
  //   NAND
  //   NOR
  //   XNOR
  //   NOT
endmodule
