// Logisim project altodesempenho.circ as structural Verilog: 1 circuit, main circuit main
module main (
  input  _0,
  input  b3,
  input  b2,
  input  b2_2,
  input  b0,
  input  a3,
  input  a2,
  input  a1,
  input  a0,
  output c4,
  output s3,
  output s2,
  output s1,
  output s0
);

  wire and_1_out, and_2_out, and_3_out, and_4_out, and_5_out, and_6_out, and_7_out, and_8_out, C2_out,
       C3_out, G1_out, G2_out, g3_out, not_1_out, or_2_out, P1_out, P2_out, p3_out, xor_1_out, xor_2_out,
       xor_3_out, xor_4_out;

  xor xor_1 (xor_1_out, _0, b3);
  and and_1 (and_1_out, P1_out, P2_out, p3_out, or_2_out);
  and and_2 (and_2_out, G1_out, P2_out, p3_out);
  or p3 (p3_out, xor_1_out, a3);
  and g3 (g3_out, xor_1_out, a3);
  and and_3 (and_3_out, p3_out, G2_out);
  or or_1 (c4, and_1_out, and_2_out, and_3_out, g3_out);
  xor xor_2 (xor_2_out, _0, b2);
  or P2 (P2_out, xor_2_out, a2);
  and and_4 (and_4_out, P2_out, P1_out, or_2_out);
  and and_5 (and_5_out, P2_out, G1_out);
  somador1bit somador1bit_1 (.C_in(C3_out), .Entrada_bit_1(a3), .Entrada_bit_2(xor_1_out), .P(s3));  // open: Co
  and G2 (G2_out, xor_2_out, a2);
  or C3 (C3_out, and_4_out, and_5_out, G2_out);
  xor xor_3 (xor_3_out, _0, b2_2);
  somador1bit somador1bit_2 (.C_in(C2_out), .Entrada_bit_1(a2), .Entrada_bit_2(xor_2_out), .P(s2));  // open: Co
  and G1 (G1_out, xor_3_out, a1);
  or P1 (P1_out, xor_3_out, a1);
  and and_6 (and_6_out, or_2_out, P1_out);
  or C2 (C2_out, and_6_out, G1_out);
  somador1bit somador1bit_3 (.C_in(or_2_out), .Entrada_bit_1(a1), .Entrada_bit_2(xor_3_out), .P(s1));  // open: Co
  xor xor_4 (xor_4_out, _0, b0);
  not not_1 (not_1_out, b0);
  and and_7 (and_7_out, a0, b0);
  and and_8 (and_8_out, not_1_out, _0);
  or or_2 (or_2_out, and_7_out, and_8_out);
  somador1bit somador1bit_4 (.C_in(_0), .Entrada_bit_1(a0), .Entrada_bit_2(xor_4_out), .P(s0));  // open: Co
endmodule
