// Logisim project altodesempenhonewCARRY.circ as structural Verilog: 1 circuit, main circuit main
module main (
  input  C0,
  input  b3,
  input  b2,
  input  b2_2,
  input  b0,
  input  b7,
  input  b6,
  input  b5,
  input  b4,
  input  a7,
  input  a6,
  input  a5,
  input  a4,
  input  a3,
  input  a2,
  input  a1,
  input  a0,
  output s5,
  output s7,
  output s6,
  output s4,
  output s3,
  output s2,
  output s1,
  output s0,
  output c7
);

  wire _0_g, _0_p, _1_g, _1_p, _2_g, _2_p, _3_g, _3_p, _4_g, _4_p, _5_g, _5_p, _6_g, _6_p, and_1_out,
       and_2_out, and_3_out, and_4_out, and_5_out, and_6_out, and_7_out, and_8_out, and_9_out, and_10_out,
       and_11_out, and_12_out, and_13_out, and_14_out, and_15_out, and_16_out, and_17_out, and_18_out,
       and_19_out, and_20_out, and_21_out, and_22_out, and_23_out, and_24_out, and_25_out, and_26_out,
       and_27_out, and_28_out, C1_out, C2_out, C3_out, C4_out, C5_out, C6_out, C7_out, xor_1_out, xor_2_out,
       xor_3_out, xor_4_out, xor_5_out, xor_6_out, xor_7_out, xor_8_out;

  xor xor_1 (xor_1_out, b7, C0);
  and and_1 (and_1_out, _6_p, _5_g);
  and and_2 (and_2_out, _6_p, _5_p, _4_p, _3_g);
  and and_3 (and_3_out, _6_p, _5_p, _4_g);
  and and_4 (and_4_out, _6_p, _5_p, _4_p, _3_p, _2_g);
  somador1bit somador1bit_1 (.C_in(C7_out), .Entrada_bit_1(a7), .Entrada_bit_2(xor_1_out), .Co(c7), .P(s7));
  and and_5 (and_5_out, _6_p, _5_p, _4_p, _3_p, _2_p, _1_g);
  or u_C7 (C7_out, _6_g, and_1_out, and_3_out, and_2_out, and_4_out, and_5_out, and_6_out, and_7_out);
  and and_6 (and_6_out, _6_p, _5_p, _4_p, _3_p, _2_p, _1_p, _0_g);
  and and_7 (and_7_out, _6_p, _5_p, _4_p, _3_p, _2_p, _1_p, _0_p, C0);
  pg _6 (.A(a6), .B(xor_2_out), .P(_6_p), .G(_6_g));
  xor xor_2 (xor_2_out, b6, C0);
  and and_8 (and_8_out, _5_p, _4_g);
  and and_9 (and_9_out, _5_p, _4_p, _3_p, _2_g);
  and and_10 (and_10_out, _5_p, _4_p, _3_g);
  somador1bit somador1bit_2 (.C_in(C6_out), .Entrada_bit_1(a6), .Entrada_bit_2(xor_2_out), .P(s6));  // open: Co
  and and_11 (and_11_out, _5_p, _4_p, _3_p, _2_p, _1_g);
  or C6 (C6_out, _5_g, and_8_out, and_10_out, and_9_out, and_11_out, and_12_out, and_13_out);
  pg _5 (.A(a5), .B(xor_3_out), .P(_5_p), .G(_5_g));
  and and_12 (and_12_out, _5_p, _4_p, _3_p, _2_p, _1_p, _0_g);
  and and_13 (and_13_out, _5_p, _4_p, _3_p, _2_p, _1_p, _0_p, C0);
  xor xor_3 (xor_3_out, C0, b5);
  and and_14 (and_14_out, _4_p, _3_g);
  somador1bit somador1bit_3 (.C_in(C5_out), .Entrada_bit_1(a5), .Entrada_bit_2(xor_3_out), .P(s5));  // open: Co
  and and_15 (and_15_out, _4_p, _3_p, _2_p, _1_g);
  and and_16 (and_16_out, _4_p, _3_p, _2_g);
  and and_17 (and_17_out, _4_p, _3_p, _2_p, _1_p, _0_g);
  or C5 (C5_out, _4_g, and_14_out, and_16_out, and_15_out, and_17_out, and_18_out);
  xor xor_4 (xor_4_out, C0, b4);
  pg _4 (.A(a4), .B(xor_4_out), .P(_4_p), .G(_4_g));
  and and_18 (and_18_out, _4_p, _3_p, _2_p, _1_p, _0_p, C0);
  and and_19 (and_19_out, _3_p, _2_g);
  and and_20 (and_20_out, _3_p, _2_p, _1_g);
  somador1bit somador1bit_4 (.C_in(C4_out), .Entrada_bit_1(a4), .Entrada_bit_2(xor_4_out), .P(s4));  // open: Co
  xor xor_5 (xor_5_out, C0, b3);
  pg _3 (.A(a3), .B(xor_5_out), .P(_3_p), .G(_3_g));
  and and_21 (and_21_out, _3_p, _2_p, _1_p, _0_g);
  and and_22 (and_22_out, _3_p, _2_p, _1_p, _0_p, C0);
  or C4 (C4_out, _3_g, and_19_out, and_20_out, and_21_out, and_22_out);
  xor xor_6 (xor_6_out, C0, b2);
  pg _2 (.A(a2), .B(xor_6_out), .P(_2_p), .G(_2_g));
  and and_23 (and_23_out, _2_p, _1_g);
  and and_24 (and_24_out, _2_p, _1_p, _0_g);
  somador1bit somador1bit_5 (.C_in(C3_out), .Entrada_bit_1(a3), .Entrada_bit_2(xor_5_out), .P(s3));  // open: Co
  and and_25 (and_25_out, _2_p, _1_p, _0_p, C0);
  or C3 (C3_out, _2_g, and_23_out, and_24_out, and_25_out);
  xor xor_7 (xor_7_out, C0, b2_2);
  somador1bit somador1bit_6 (.C_in(C2_out), .Entrada_bit_1(a2), .Entrada_bit_2(xor_6_out), .P(s2));  // open: Co
  pg _1 (.A(a1), .B(xor_7_out), .P(_1_p), .G(_1_g));
  and and_26 (and_26_out, _1_p, _0_g);
  or C2 (C2_out, _1_g, and_26_out, and_27_out);
  and and_27 (and_27_out, _1_p, _0_p, C0);
  somador1bit somador1bit_7 (.C_in(C1_out), .Entrada_bit_1(a1), .Entrada_bit_2(xor_7_out), .P(s1));  // open: Co
  xor xor_8 (xor_8_out, C0, b0);
  pg _0 (.A(a0), .B(xor_8_out), .P(_0_p), .G(_0_g));
  and and_28 (and_28_out, _0_p, C0);
  or C1 (C1_out, _0_g, and_28_out);
  somador1bit somador1bit_8 (.C_in(C0), .Entrada_bit_1(a0), .Entrada_bit_2(xor_8_out), .P(s0));  // open: Co
endmodule
