// Logisim project 1bitripplecarry.circ as structural Verilog: 1 circuit, main circuit somador1bit
module somador1bit (
  input  C_in,
  input  Entrada_bit_1,
  input  Entrada_bit_2,
  output P,
  output Co
);

  wire and_1_out, and_2_out, and_3_out, xor_1_out;

  xor xor_1 (xor_1_out, Entrada_bit_1, C_in);
  and and_1 (and_1_out, Entrada_bit_1, C_in);
  and and_2 (and_2_out, Entrada_bit_1, Entrada_bit_2);
  and and_3 (and_3_out, Entrada_bit_2, C_in);
  xor Saida (P, Entrada_bit_2, xor_1_out);
  or C_out (Co, and_1_out, and_2_out, and_3_out);
endmodule
