// Logisim project SomSubRC8bits.circ as structural Verilog: 1 circuit, main circuit Somador e subtrator 8bits
module Somador_e_subtrator_8bits (
  input  a7,
  input  a6,
  input  a5,
  input  a4,
  input  a3,
  input  a2,
  input  a1,
  input  a0,
  input  b7,
  input  b6,
  input  b5,
  input  b4,
  input  b3,
  input  b2,
  input  b1,
  input  b0,
  input  \soma_ou_subtração ,
  output Carry,
  output s7,
  output s6,
  output s5,
  output s4,
  output s3,
  output s2,
  output s1,
  output s0
);

  wire somador1bit_2_co, somador1bit_3_co, somador1bit_4_co, somador1bit_5_co, somador1bit_6_co,
       somador1bit_7_co, somador1bit_8_co, xor_1_out, xor_2_out, xor_3_out, xor_4_out, xor_5_out, xor_6_out,
       xor_7_out, xor_8_out;

  xor xor_1 (xor_1_out, b7, \soma_ou_subtração );
  xor xor_2 (xor_2_out, b6, \soma_ou_subtração );
  somador1bit somador1bit_1 (
    .C_in(somador1bit_2_co), .Entrada_bit_1(a7), .Entrada_bit_2(xor_1_out), .Co(Carry), .P(s7));
  xor xor_3 (xor_3_out, b5, \soma_ou_subtração );
  somador1bit somador1bit_2 (
    .C_in(somador1bit_3_co), .Entrada_bit_1(a6), .Entrada_bit_2(xor_2_out), .Co(somador1bit_2_co), .P(s6));
  xor xor_4 (xor_4_out, b4, \soma_ou_subtração );
  somador1bit somador1bit_3 (
    .C_in(somador1bit_4_co), .Entrada_bit_1(a5), .Entrada_bit_2(xor_3_out), .Co(somador1bit_3_co), .P(s5));
  xor xor_5 (xor_5_out, b3, \soma_ou_subtração );
  somador1bit somador1bit_4 (
    .C_in(somador1bit_5_co), .Entrada_bit_1(a4), .Entrada_bit_2(xor_4_out), .Co(somador1bit_4_co), .P(s4));
  xor xor_6 (xor_6_out, b2, \soma_ou_subtração );
  somador1bit somador1bit_5 (
    .C_in(somador1bit_6_co), .Entrada_bit_1(a3), .Entrada_bit_2(xor_5_out), .Co(somador1bit_5_co), .P(s3));
  xor xor_7 (xor_7_out, b1, \soma_ou_subtração );
  somador1bit somador1bit_6 (
    .C_in(somador1bit_7_co), .Entrada_bit_1(a2), .Entrada_bit_2(xor_6_out), .Co(somador1bit_6_co), .P(s2));
  xor xor_8 (xor_8_out, b0, \soma_ou_subtração );
  somador1bit somador1bit_7 (
    .C_in(somador1bit_8_co), .Entrada_bit_1(a1), .Entrada_bit_2(xor_7_out), .Co(somador1bit_7_co), .P(s1));
  somador1bit somador1bit_8 (
    .C_in(\soma_ou_subtração ), .Entrada_bit_1(a0), .Entrada_bit_2(xor_8_out), .Co(somador1bit_8_co), .P(s0));
endmodule
