// Logisim project somador 8bits alto desempenho.circ as structural Verilog: 1 circuit, main circuit main
module main (
  input  a3,
  input  a2,
  input  a1,
  input  a0,
  input  b3,
  input  b2,
  input  b2_2,
  input  b0,
  input  _0,
  output c4,
  output s3,
  output s2,
  output s1,
  output s0
);

  wire and_1_out, and_2_out, and_3_out, and_4_out, and_5_out, and_6_out, C1_out, C2_out, C3_out, G1_out,
       G2_out, g3_out, P1_out, P2_out, p3_out;

  and and_1 (and_1_out, P1_out, P2_out, p3_out, C1_out);
  or p3 (p3_out, b3, a3);
  and and_2 (and_2_out, p3_out, G2_out);
  and and_3 (and_3_out, G1_out, P2_out, p3_out);
  or or_1 (c4, and_1_out, and_3_out, and_2_out, g3_out);
  and g3 (g3_out, b3, a3);
  or P2 (P2_out, b2, a2);
  and and_4 (and_4_out, P2_out, P1_out, C1_out);
  and and_5 (and_5_out, P2_out, G1_out);
  somador1bit somador1bit_1 (.C_in(C3_out), .Entrada_bit_1(a3), .Entrada_bit_2(b3), .P(s3));  // open: Co
  and G2 (G2_out, b2, a2);
  or C3 (C3_out, and_4_out, and_5_out, G2_out);
  somador1bit somador1bit_2 (.C_in(C2_out), .Entrada_bit_1(a2), .Entrada_bit_2(b2), .P(s2));  // open: Co
  or P1 (P1_out, b2_2, a1);
  and and_6 (and_6_out, C1_out, P1_out);
  or C2 (C2_out, and_6_out, G1_out);
  and G1 (G1_out, b2_2, a1);
  somador1bit somador1bit_3 (.C_in(C1_out), .Entrada_bit_1(a1), .Entrada_bit_2(b2_2), .P(s1));  // open: Co
  and C1 (C1_out, b0, a0);
  somador1bit somador1bit_4 (.C_in(_0), .Entrada_bit_1(a0), .Entrada_bit_2(b0), .P(s0));  // open: Co
endmodule
